# Fritzing sketch PiZero_gpio_led_sw (saved by Fritzing 0.9.3b)
breadboards: 1

parts:
  LED2 = LED - 5mm [color="Red (633nm)" package="5 mm [THT]"]
  R2 = Resistor [tolerance=±5% resistance=1k part_number="茶黒赤金　　" package="2512 [SMD]"]
  MCU1 = Raspberry Pi Zero
  S1 = Pushbutton [package=THT]

nets:
  N1: LED2.cathode, MCU1.pin_30, MCU1.pin_34, S1.leg1
  N2: LED2.anode, R2.Pin_0
  N3: R2.Pin_1, MCU1.pin_37
  N4: MCU1.pin_29, S1.leg0

notes:
  LED足の長いほう
